# Fritzing sketch pinset (saved by Fritzing 0.9.3b)
breadboards: 2

parts:
  부품1 = Arduino Mega 2560 (Rev3)
  부품2 = Arduino Mega 2560 (Rev3)
  S1 = Pushbutton [package="[THT]"]
  S7 = Pushbutton [package="[THT]"]
  R1 = Resistor [tolerance=±5% resistance=220 package=THT]
  S8 = Pushbutton [package="[THT]"]
  R2 = Resistor [tolerance=±5% resistance=220 package=THT]
  S9 = Pushbutton [package="[THT]"]
  R3 = Resistor [tolerance=±5% resistance=220 package=THT]
  R4 = Resistor [tolerance=±5% resistance=220 package=THT]
  R5 = Resistor [tolerance=±5% resistance=220 package=THT]
  S10 = Pushbutton [package="[THT]"]
  S11 = Pushbutton [package="[THT]"]
  S12 = Pushbutton [package="[THT]"]
  S13 = Pushbutton [package="[THT]"]
  R6 = Resistor [tolerance=±5% resistance=220 package=THT]
  R7 = Resistor [tolerance=±5% resistance=220 package=THT]
  R8 = Resistor [tolerance=±5% resistance=220 package=THT]
  R9 = Trimmer Potentiometer [maximum_resistance=10kΩ package=THT]
  LED1 = LED - 5mm [color="Red (633nm)" package="5 mm [THT]"]
  LED2 = LED - 5mm [color="Red (633nm)" package="5 mm [THT]"]
  LED3 = LED - 5mm [color="Red (633nm)" package="5 mm [THT]"]
  LED4 = LED - 5mm [color="Red (633nm)" package="5 mm [THT]"]
  LED5 = LED - 5mm [color="Red (633nm)" package="5 mm [THT]"]
  LED6 = LED - 5mm [color="Red (633nm)" package="5 mm [THT]"]
  LED7 = LED - 5mm [color="Red (633nm)" package="5 mm [THT]"]
  LED8 = LED - 5mm [color="Red (633nm)" package="5 mm [THT]"]

nets:
  N1: 부품1.A0, R9.wiper
  N2: 부품1.D21/SCL, 부품1.SCL, 부품2.D21/SCL
  N3: 부품1.D20/SDA, 부품1.SDA, 부품2.D20/SDA
  N4: 부품1.GND, LED1.cathode, LED2.cathode, LED3.cathode, LED4.cathode, LED5.cathode, LED6.cathode, LED7.cathode, LED8.cathode
  N5: 부품1.D23, 부품2.D27
  N6: 부품1.D25, 부품2.D25
  N7: 부품1.D29, S13.Pin_3, S13.Pin_4, R8.Pin_1
  N8: 부품1.D31, S1.Pin_3, S1.Pin_4, R1.Pin_1
  N9: 부품1.D33, S8.Pin_3, S8.Pin_4, R2.Pin_1
  N10: 부품1.D35, S9.Pin_3, S9.Pin_4, R3.Pin_1
  N11: 부품1.D37, S7.Pin_3, S7.Pin_4, R4.Pin_1
  N12: 부품1.D39, R5.Pin_1, S10.Pin_3, S10.Pin_4
  N13: 부품1.D41, S11.Pin_3, S11.Pin_4, R6.Pin_1
  N14: 부품1.D43, S12.Pin_3, S12.Pin_4, R7.Pin_1
  N15: 부품1.D46, LED8.anode
  N16: 부품1.D47, LED5.anode
  N17: 부품1.D48, LED7.anode
  N18: 부품1.D49, LED4.anode
  N19: 부품1.D50, LED6.anode
  N20: 부품1.D51, LED3.anode
  N21: 부품1.D52, LED1.anode
  N22: 부품1.D53, LED2.anode
  N23: 부품2.5V, R1.Pin_0, R2.Pin_0, R3.Pin_0, R4.Pin_0, R5.Pin_0, R6.Pin_0, R7.Pin_0, R8.Pin_0
  N24: 부품2.GND, S1.Pin_1, S1.Pin_2, S7.Pin_1, S7.Pin_2, S8.Pin_1, S8.Pin_2, S9.Pin_1, S9.Pin_2, S10.Pin_1, S10.Pin_2, S11.Pin_1, S11.Pin_2, S12.Pin_1, S12.Pin_2, S13.Pin_1, S13.Pin_2, R9.leg2
